// Logisim project 25CSB1A78_DewanshRajSah_COA.circ as structural Verilog: 6 circuits, main circuit main
module main (
  input  reserved_1,
  input  clock,
  input  car_enter,
  input  [2:0] exit_select,
  input  car_exit,
  output [5:0] parking_fee,
  output parking_full,
  output parking_empty
);

  wire and_1_out, and_2_out, and_3_out, d_ff_1_q, decoder_1_out0, decoder_1_out1, decoder_1_out2,
       decoder_1_out3, decoder_1_out4, decoder_1_out5, decoder_1_out6, decoder_1_out7, decoder_2_out0,
       decoder_2_out1, decoder_2_out2, decoder_2_out3, decoder_2_out4, decoder_2_out5, decoder_2_out6,
       decoder_2_out7, entry_exit_control_1_out_17, entry_exit_control_1_out_18, entry_exit_control_1_out_19,
       entry_exit_control_1_out_20, entry_exit_control_1_out_21, entry_exit_control_1_out_22,
       entry_exit_control_1_out_23, entry_exit_control_1_out_24, entry_exit_control_2_out_17,
       entry_exit_control_2_out_18, entry_exit_control_2_out_19, entry_exit_control_2_out_20,
       entry_exit_control_2_out_21, entry_exit_control_2_out_22, entry_exit_control_2_out_23,
       entry_exit_control_2_out_24, full_out, invalid_exit_1_out_17, invalid_exit_1_out_18,
       invalid_exit_1_out_19, invalid_exit_1_out_20, invalid_exit_1_out_21, invalid_exit_1_out_22,
       invalid_exit_1_out_23, invalid_exit_1_out_24, not_1_out, not_2_out, not_3_out, not_4_out, not_5_out,
       not_6_out, not_7_out, not_8_out, not_9_out, not_10_out, or_1_out, or_2_out,
       parkingslot_1_slot_occupied, parkingslot_2_slot_occupied, parkingslot_3_slot_occupied,
       parkingslot_4_slot_occupied, parkingslot_6_slot_occupied, parkingslot_7_slot_occupied,
       parkingslot_8_slot_occupied;
  wire [2:0] priority_encoder_1_out;
  wire [3:0] counter_1_q, counter_2_q, parkingtimer_1_duration;

  Decoder #(.select(3)) decoder_1 (
    .out0(decoder_1_out0), .out1(decoder_1_out1), .out2(decoder_1_out2), .out3(decoder_1_out3),
    .out4(decoder_1_out4), .out5(decoder_1_out5), .out6(decoder_1_out6), .out7(decoder_1_out7),
    .sel(exit_select), .en(1'b1));
  D_Flip_Flop d_ff_1 (.clk(clock), .D(and_1_out), .Q(d_ff_1_q));  // open: Qn, preset, en, reset
  or or_1 (or_1_out, entry_exit_control_2_out_17, d_ff_1_q);
  not not_1 (not_1_out, entry_exit_control_1_out_17);
  LED led_1 (.in(parkingslot_1_slot_occupied));
  parkingSlot parkingslot_1 (
    .s_entry(entry_exit_control_2_out_18), .clock(clock), .s_exit(entry_exit_control_1_out_18),
    .slot_occupied(parkingslot_1_slot_occupied));
  LED led_2 (.in(parkingslot_2_slot_occupied));
  parkingSlot parkingslot_2 (
    .s_entry(entry_exit_control_2_out_19), .clock(clock), .s_exit(entry_exit_control_1_out_19),
    .slot_occupied(parkingslot_2_slot_occupied));
  LED led_3 (.in(parkingslot_3_slot_occupied));
  parkingSlot parkingslot_3 (
    .s_entry(entry_exit_control_2_out_20), .clock(clock), .s_exit(entry_exit_control_1_out_20),
    .slot_occupied(parkingslot_3_slot_occupied));
  LED led_4 (.in(parkingslot_4_slot_occupied));
  parkingSlot parkingslot_4 (
    .s_entry(entry_exit_control_2_out_21), .clock(clock), .s_exit(entry_exit_control_1_out_21),
    .slot_occupied(parkingslot_4_slot_occupied));
  entry_exit_control entry_exit_control_1 (
    .in_1(car_exit), .in_2(decoder_1_out0), .in_3(car_exit), .in_4(decoder_1_out1), .in_5(car_exit),
    .in_6(decoder_1_out2), .in_7(car_exit), .in_8(decoder_1_out3), .in_9(car_exit), .in_10(decoder_1_out4),
    .in_11(car_exit), .in_12(decoder_1_out5), .in_13(car_exit), .in_14(decoder_1_out6), .in_15(car_exit),
    .in_16(decoder_1_out7), .out_17(entry_exit_control_1_out_17), .out_18(entry_exit_control_1_out_18),
    .out_19(entry_exit_control_1_out_19), .out_20(entry_exit_control_1_out_20),
    .out_21(entry_exit_control_1_out_21), .out_22(entry_exit_control_1_out_22),
    .out_23(entry_exit_control_1_out_23), .out_24(entry_exit_control_1_out_24));
  parkingSlot parkingslot_5 (
    .s_entry(entry_exit_control_2_out_17), .clock(clock), .s_exit(entry_exit_control_1_out_17),
    .slot_occupied(d_ff_1_q));
  and and_1 (and_1_out, or_1_out, not_1_out);
  LED led_5 (.in(d_ff_1_q));
  parkingSlot parkingslot_6 (
    .s_entry(entry_exit_control_2_out_22), .clock(clock), .s_exit(entry_exit_control_1_out_22),
    .slot_occupied(parkingslot_6_slot_occupied));
  parkingSlot parkingslot_7 (
    .s_entry(entry_exit_control_2_out_23), .clock(clock), .s_exit(entry_exit_control_1_out_23),
    .slot_occupied(parkingslot_7_slot_occupied));
  parkingSlot parkingslot_8 (
    .s_entry(entry_exit_control_2_out_24), .clock(clock), .s_exit(entry_exit_control_1_out_24),
    .slot_occupied(parkingslot_8_slot_occupied));
  parkingTimer parkingtimer_1 (
    .timer_reset(entry_exit_control_1_out_24), .slot_occupied(parkingslot_8_slot_occupied),
    .timer_clock(clock), .duration(parkingtimer_1_duration));
  LED led_6 (.in(parkingslot_6_slot_occupied));
  LED led_7 (.in(parkingslot_7_slot_occupied));
  LED led_8 (.in(parkingslot_8_slot_occupied));
  Hex_Digit_Display hex_digit_display_1 (.value(parkingtimer_1_duration));  // open: dp
  Counter #(.width(4), .max('h8)) counter_1 (
    .load(car_exit), .D(4'b0000), .count(car_enter), .Q(counter_1_q), .clk(clock));  // open: carry, clr
  LED led_9 (.in(reserved_1));
  feeCalculator feecalculator_1 (.duration(parkingtimer_1_duration), .parking_fee(parking_fee));  // open: temp_fee
  or or_2 (or_2_out, car_enter, car_exit);
  Counter #(.width(4), .max('h8)) counter_2 (
    .load(car_enter), .D(4'b1000), .count(or_2_out), .Q(counter_2_q), .clk(clock));  // open: carry, clr
  Hex_Digit_Display hex_digit_display_2 (.value(counter_1_q));  // open: dp
  not not_2 (not_2_out, reserved_1);
  not not_3 (not_3_out, d_ff_1_q);
  not not_4 (not_4_out, parkingslot_1_slot_occupied);
  not not_5 (not_5_out, parkingslot_2_slot_occupied);
  not not_6 (not_6_out, parkingslot_3_slot_occupied);
  not not_7 (not_7_out, parkingslot_4_slot_occupied);
  not not_8 (not_8_out, parkingslot_6_slot_occupied);
  not not_9 (not_9_out, parkingslot_7_slot_occupied);
  not not_10 (not_10_out, parkingslot_8_slot_occupied);
  Hex_Digit_Display hex_digit_display_3 (.value(counter_2_q));  // open: dp
  and and_2 (and_2_out, not_3_out, not_2_out);
  Priority_Encoder priority_encoder_1 (
    .in0(and_2_out), .in1(not_4_out), .in2(not_5_out), .in3(not_6_out), .in4(not_7_out), .in5(not_8_out),
    .in6(not_9_out), .in7(not_10_out), .out(priority_encoder_1_out), .en_in(1'b1));  // open: gs, en_out
  invalid_exit invalid_exit_1 (
    .in_1(d_ff_1_q), .in_2(car_exit), .in_3(parkingslot_1_slot_occupied), .in_4(car_exit),
    .in_5(parkingslot_2_slot_occupied), .in_6(car_exit), .in_7(parkingslot_3_slot_occupied), .in_8(car_exit),
    .in_9(parkingslot_4_slot_occupied), .in_10(car_exit), .in_11(parkingslot_6_slot_occupied),
    .in_12(car_exit), .in_13(parkingslot_7_slot_occupied), .in_14(car_exit),
    .in_15(parkingslot_8_slot_occupied), .in_16(car_exit), .out_17(invalid_exit_1_out_17),
    .out_18(invalid_exit_1_out_18), .out_19(invalid_exit_1_out_19), .out_20(invalid_exit_1_out_20),
    .out_21(invalid_exit_1_out_21), .out_22(invalid_exit_1_out_22), .out_23(invalid_exit_1_out_23),
    .out_24(invalid_exit_1_out_24));
  LED led_10 (.in(invalid_exit_1_out_17));
  LED led_11 (.in(invalid_exit_1_out_18));
  LED led_12 (.in(invalid_exit_1_out_19));
  LED led_13 (.in(invalid_exit_1_out_20));
  LED led_14 (.in(invalid_exit_1_out_21));
  LED led_15 (.in(invalid_exit_1_out_22));
  LED led_16 (.in(invalid_exit_1_out_23));
  LED led_17 (.in(invalid_exit_1_out_24));
  // Probe on priority_encoder_1_out
  not not_11 (parking_full, full_out);
  or full (full_out, not_3_out, not_4_out, not_5_out, not_6_out, not_7_out, not_8_out, not_9_out, not_10_out);
  and empty (parking_empty, not_3_out, not_4_out, not_5_out, not_6_out, not_7_out, not_8_out, not_9_out, not_10_out);
  Decoder #(.select(3)) decoder_2 (
    .out0(decoder_2_out0), .out1(decoder_2_out1), .out2(decoder_2_out2), .out3(decoder_2_out3),
    .out4(decoder_2_out4), .out5(decoder_2_out5), .out6(decoder_2_out6), .out7(decoder_2_out7),
    .sel(priority_encoder_1_out), .en(1'b1));
  LED led_18 (.in(and_3_out));
  and and_3 (and_3_out, car_enter, parking_full);
  // Probe on decoder_2_out0
  // Probe on decoder_2_out1
  // Probe on decoder_2_out2
  // Probe on decoder_2_out3
  // Probe on decoder_2_out4
  // Probe on decoder_2_out5
  // Probe on decoder_2_out6
  // Probe on decoder_2_out7
  entry_exit_control entry_exit_control_2 (
    .in_1(decoder_2_out0), .in_2(car_enter), .in_3(decoder_2_out1), .in_4(car_enter), .in_5(decoder_2_out2),
    .in_6(car_enter), .in_7(decoder_2_out3), .in_8(car_enter), .in_9(decoder_2_out4), .in_10(car_enter),
    .in_11(decoder_2_out5), .in_12(car_enter), .in_13(decoder_2_out6), .in_14(car_enter),
    .in_15(decoder_2_out7), .in_16(car_enter), .out_17(entry_exit_control_2_out_17),
    .out_18(entry_exit_control_2_out_18), .out_19(entry_exit_control_2_out_19),
    .out_20(entry_exit_control_2_out_20), .out_21(entry_exit_control_2_out_21),
    .out_22(entry_exit_control_2_out_22), .out_23(entry_exit_control_2_out_23),
    .out_24(entry_exit_control_2_out_24));

  // Notes on the sheet:
  //   s1_entry
  //   exit decoder
  //   flip flop
  //   s1_exit
  //   s2_entry
  //   s2_exit
  //   s3_entry
  //   s3_exit
  //   s4_entry
  //   s4_exit
  //   s5_entry
  //   slot_2
  //   slot_3
  //   slot_4
  //   slot_5
  //   s5_exit
  //   exit
  //   entry / exit control
  //   slot_1 (reserved)
  //   s6_entry
  //   s6_exit
  //   s7_entry
  //   s7_exit
  //   s8_entry
  //   s8_exit
  //   slot_6
  //   slot_7
  //   slot_8
  //   slot_8_timer
  //   occupied counter
  //   slot_8_fee
  //   slot_1 reserved
  //   vacancy_1
  //   vacancy_2
  //   vacancy_3
  //   vacancy_4
  //   vacancy_5
  //   vacancy_6
  //   vacancy_7
  //   vacancy_8
  //   available counter
  //   not_reserved_1
  //   invalid_exit
  //   slot no.
  //   slot priority (reverse_order)
  //   slot 1
  //   slot 2
  //   slot 3
  //   slot 4
  //   slot 5
  //   slot 6
  //   slot 7
  //   slot 8
  //   entry decoder
  //   invalid_entry
  //   entry / exit control
  //   slot 1
  //   slot 2
  //   slot 3
  //   slot 4
  //   slot 5
  //   slot 6
  //   slot 7
  //   slot 8
  //   entry
endmodule

module parkingSlot (
  input  s_entry,
  input  clock,
  input  s_exit,
  output slot_occupied
);

  wire and_1_out, not_1_out, or_1_out;

  LED led_1 (.in(slot_occupied));
  D_Flip_Flop d_ff_1 (.clk(clock), .D(and_1_out), .Q(slot_occupied));  // open: Qn, preset, en, reset
  // Probe on and_1_out
  or or_1 (or_1_out, s_entry, slot_occupied);
  not not_1 (not_1_out, s_exit);
  and and_1 (and_1_out, or_1_out, not_1_out);
  // Probe on nothing

  // Notes on the sheet:
  //   flip flop
endmodule

module entry_exit_control (
  input  in_1,
  input  in_2,
  input  in_3,
  input  in_4,
  input  in_5,
  input  in_6,
  input  in_7,
  input  in_8,
  input  in_9,
  input  in_10,
  input  in_11,
  input  in_12,
  input  in_13,
  input  in_14,
  input  in_15,
  input  in_16,
  output out_17,
  output out_18,
  output out_19,
  output out_20,
  output out_21,
  output out_22,
  output out_23,
  output out_24
);

  and and_1 (out_17, in_1, in_2);
  and and_2 (out_18, in_3, in_4);
  and and_3 (out_19, in_5, in_6);
  and and_4 (out_20, in_7, in_8);
  and and_5 (out_21, in_9, in_10);
  and and_6 (out_22, in_11, in_12);
  and and_7 (out_23, in_13, in_14);
  and and_8 (out_24, in_15, in_16);
endmodule

module invalid_exit (
  input  in_1,
  input  in_2,
  input  in_3,
  input  in_4,
  input  in_5,
  input  in_6,
  input  in_7,
  input  in_8,
  input  in_9,
  input  in_10,
  input  in_11,
  input  in_12,
  input  in_13,
  input  in_14,
  input  in_15,
  input  in_16,
  output out_17,
  output out_18,
  output out_19,
  output out_20,
  output out_21,
  output out_22,
  output out_23,
  output out_24
);

  wire not_1_out, not_2_out, not_3_out, not_4_out, not_5_out, not_6_out, not_7_out, not_8_out;

  not not_1 (not_1_out, in_1);
  not not_2 (not_2_out, in_3);
  not not_3 (not_3_out, in_5);
  not not_4 (not_4_out, in_7);
  not not_5 (not_5_out, in_9);
  not not_6 (not_6_out, in_11);
  not not_7 (not_7_out, in_13);
  not not_8 (not_8_out, in_15);
  and and_1 (out_17, not_1_out, in_2);
  and and_2 (out_18, not_2_out, in_4);
  and and_3 (out_19, not_3_out, in_6);
  and and_4 (out_20, not_4_out, in_8);
  and and_5 (out_21, not_5_out, in_10);
  and and_6 (out_22, not_6_out, in_12);
  and and_7 (out_23, not_7_out, in_14);
  and and_8 (out_24, not_8_out, in_16);
endmodule

module parkingTimer (
  input  timer_reset,
  input  slot_occupied,
  input  timer_clock,
  output [3:0] duration
);

  Counter #(.width(4), .max('hf)) counter_1 (
    .load(timer_reset), .D(4'b0000), .count(slot_occupied), .Q(duration), .clk(timer_clock));  // open: carry, clr
  Hex_Digit_Display hex_digit_display_1 (.value(duration));  // open: dp
endmodule

module feeCalculator (
  input  [3:0] duration,
  output [5:0] temp_fee,
  output [5:0] parking_fee
);

  wire comparator_1_lt, comparator_2_lt, not_1_out, not_2_out;

  Comparator #(.width(4), .mode("unsigned")) comparator_1 (
    .a(duration), .b(4'b0100), .lt(comparator_1_lt));  // open: gt, eq
  Comparator #(.width(4), .mode("unsigned")) comparator_2 (
    .a(duration), .b(4'b1000), .lt(comparator_2_lt));  // open: gt, eq
  not not_1 (not_1_out, comparator_1_lt);
  not not_2 (not_2_out, comparator_2_lt);
  Multiplexer #(.width(6), .enable("false")) multiplexer_1 (
    .in0(6'b001010), .in1(6'b010100), .out(temp_fee), .sel(not_1_out));
  Multiplexer #(.width(6), .enable("false")) multiplexer_2 (
    .in0(temp_fee), .in1(6'b011110), .out(parking_fee), .sel(not_2_out));

  // Notes on the sheet:
  //   threshold_4
  //   rs. 10
  //   rs. 20
  //   threshold_8
  //   rs. 30
endmodule
